# Fritzing sketch uno (saved by Fritzing 0.8.7b)
breadboards: 1

parts:
  Parte3 = Arduino XBee Shield
  S1 = SWITCH-MOMENTARY-2 [package=tactile-pth-12mm]
  U1 = Thumb Joystick [package=joystick]
  S2 = SWITCH-MOMENTARY-2 [package=tactile-pth-12mm]
  S3 = SWITCH-MOMENTARY-2 [package=tactile-pth-12mm]
  S4 = SWITCH-MOMENTARY-2 [package=tactile-pth-12mm]
  S5 = SWITCH-MOMENTARY-2 [package=tactile-pth-12mm]
  S6 = SWITCH-MOMENTARY-2 [package=tactile-pth-12mm]
  Parte4 = Arduino Uno (Rev3)
  R7 = Resistor [tolerance=±5% resistance=10k package=THT]
  R8 = Resistor [tolerance=±5% resistance=10k package=THT]
  R9 = Resistor [tolerance=±5% resistance=10k package=THT]
  R10 = Resistor [tolerance=±5% resistance=10k package=THT]
  R11 = Resistor [tolerance=±5% resistance=10k package=THT]
  R12 = Resistor [tolerance=±5% resistance=10k package=THT]
  R13 = Resistor [tolerance=±5% resistance=10k package=THT]

nets:
  N1: Parte3.GND, U1.H-, U1.V-, R7.Pin_0, R8.Pin_0, R9.Pin_0, R10.Pin_0, R11.Pin_0, R12.Pin_0, R13.Pin_0
  5V: Parte3.5V, S1.2, U1.SEL+, U1.V+, U1.H+, S2.2, S3.2, S4.2, S5.2, S6.2, Parte4.5V
  N2: Parte3.D8, S3.1, Parte4.D8, R10.Pin_1
  N3: Parte3.D9, S2.1, Parte4.D9_PWM, R9.Pin_1
  N4: Parte3.D10, S4.1, Parte4.D10_PWM/SS, R8.Pin_1
  N5: Parte3.D11, S1.1, Parte4.D11_PWM/MOSI, R7.Pin_1
  N6: Parte3.A0, U1.H, Parte4.A0
  N7: Parte3.A1, U1.V, Parte4.A1
  N8: Parte3.A2, U1.SEL-, Parte4.A2, R11.Pin_1
  N9: Parte3.A3, S5.1, Parte4.A3, R12.Pin_1
  N10: Parte3.A4, S6.1, Parte4.A4/SDA, R13.Pin_1
  N11: Parte3.A5, Parte4.A5/SCL
  N12: Parte3.AREF, Parte4.AREF
  N13: Parte3.D_RX, Parte4.D2
  N14: Parte3.D_TX, Parte4.D3_PWM
  N15: Parte3.D4, Parte4.D4
  N16: Parte3.D5, Parte4.D5_PWM
  N17: Parte3.D6, Parte4.D6_PWM
  N18: Parte3.D7, Parte4.D7
  N19: Parte3.D12, Parte4.D12/MISO
  N20: Parte3.D13, Parte4.D13/SCK
  N21: Parte3.RST, Parte4.RESET
  N22: Parte3.UART_RX, Parte4.D0/RX
  N23: Parte3.UART_TX, Parte4.D1/TX
  VIN: Parte3.VIN, Parte4.VIN
  N24: Parte3.N$92, Parte4.GND
